# Fritzing sketch RDM6300 (saved by Fritzing 0.9.3b)

parts:
  125_kHz_RFID_module1 = RDM6300
  Part1 = Arduino Nano (Rev3.0)
  KY-1 = Keyes Relay [package=THT]
  JACK1 = 2.1mm Barrel Jack with Terminal Block
  L1 = MagLock

nets:
  N1: 125_kHz_RFID_module1.TX, 125_kHz_RFID_module1.GND#67, Part1.D8
  N2: 125_kHz_RFID_module1.NULL, 125_kHz_RFID_module1.GND#60, Part1.GND, KY-1.ground
  +5V: 125_kHz_RFID_module1.+5V, Part1.5V, KY-1.power
  N3: Part1.D12/MISO, KY-1.signal
  N4: KY-1.NC, KY-1.NO, L1.pin2
  N5: KY-1.C, JACK1.POS
  N6: JACK1.NEG, L1.pin1

notes:
  RDM6300 reads EM4100 cards @125kHz. When a new card is detected, it is read and data sent via serial connection on the TX pin (Pin 8 shown here).
  Requires only three wires to Arduino:
  RDM6300 +5V <-> Arduino 5V
  RDM6300 GND <-> Arduino GND
  RDM6300 TX <-> Arduino Pin 8 (or other receive pin defined as Software Serial in code)
  RDM6300 ANT1 and ANT2 should be connected to the antenna (polarity is unimportant)
  The other pins on the RDM6300 board do not need to be connected... VCC and GND are duplicated, the middle pin of the block of five doesn't do anything, and the RX pin is also redundant, since the Arduino never sends data or commands *to* the RDM6300.
  Relay will be activated by LOW signal sent when correct tag ID is read
  Relay can switch any load, e.g. a 12V DC maglock

custom parts:
  RDM6300: 125 kHz RFID module (serial interface)
  Keyes Relay: The Keyes 5V relay module is suitable for SCM development, home appliance control. It uses a 5V~12V TIL control signal which can control DC / AC signal.
  MagLock: A bar-style 12V/24V maglock
